// Logisim project mef-principal.circ as structural Verilog: 5 circuits, main circuit main
module main (
  input  Clock,
  input  Start,
  input  PG,
  input  CH,
  input  RO,
  input  CQ,
  input  EB,
  output E2,
  output E1,
  output E0,
  output MOTOR,
  output EV,
  output VE,
  output ALARME
);

  wire \Lógica_de_Estado_Próximo___E0_j0 , \Lógica_de_Estado_Próximo___E0_k0 ,
       \Lógica_de_Estado_Próximo___E1_j1 , \Lógica_de_Estado_Próximo___E1_k1 ,
       \Lógica_de_Estado_Próximo___E2_j2 , \Lógica_de_Estado_Próximo___E2_k2 ;

  ff2 \Lógica_de_Estado_Próximo___E2  (
    .Start(Start), .RO(RO), .E2(E2), .E1(E1), .E0(E0), .CH(CH), .J2(\Lógica_de_Estado_Próximo___E2_j2 ),
    .K2(\Lógica_de_Estado_Próximo___E2_k2 ));
  FF1 \Lógica_de_Estado_Próximo___E1  (
    .Start(Start), .RO(RO), .E2(E2), .E0(E0), .CH(CH), .CQ(CQ), .PG(PG),
    .J1(\Lógica_de_Estado_Próximo___E1_j1 ), .K1(\Lógica_de_Estado_Próximo___E1_k1 ));
  FF0 \Lógica_de_Estado_Próximo___E0  (
    .Start(Start), .RO(RO), .E2(E2), .E1(E1), .E0(E0), .CH(CH), .CQ(CQ), .PG(PG), .EB(EB),
    .J0(\Lógica_de_Estado_Próximo___E0_j0 ), .K0(\Lógica_de_Estado_Próximo___E0_k0 ));
  Circuito_de_Saida Circuito_de_Saida (
    .Start(Start), .RO(RO), .E2(E2), .E1(E1), .E0(E0), .CH(CH), .PG(PG), .CQ(CQ), .EB(EB), .MOTOR(MOTOR),
    .EV(EV), .VE(VE), .ALARME(ALARME));
  J_K_Flip_Flop FF2 (
    .J(\Lógica_de_Estado_Próximo___E2_j2 ), .clk(Clock), .K(\Lógica_de_Estado_Próximo___E2_k2 ), .Q(E2));  // open: Qn, preset, en, reset
  J_K_Flip_Flop FF1 (
    .J(\Lógica_de_Estado_Próximo___E1_j1 ), .clk(Clock), .K(\Lógica_de_Estado_Próximo___E1_k1 ), .Q(E1));  // open: Qn, preset, en, reset
  J_K_Flip_Flop FF0 (
    .J(\Lógica_de_Estado_Próximo___E0_j0 ), .clk(Clock), .K(\Lógica_de_Estado_Próximo___E0_k0 ), .Q(E0));  // open: Qn, preset, en, reset
endmodule

module ff2 (
  input  Start,
  input  RO,
  input  E2,
  input  E1,
  input  E0,
  input  CH,
  output J2,
  output K2
);

  wire and_1_out, and_2_out, and_3_out, and_4_out, not_1_out, not_2_out, not_3_out, not_4_out;

  not not_1 (not_1_out, E2);
  not not_2 (not_2_out, E2);
  not not_3 (not_3_out, E1);
  not not_4 (not_4_out, E0);
  and and_1 (and_1_out, Start, RO, not_1_out, E1, E0);
  and and_2 (and_2_out, Start, CH, RO, not_2_out, E1);
  and and_3 (and_3_out, Start, not_3_out, E0);
  and and_4 (and_4_out, Start, E1, not_4_out);
  or or_1 (J2, and_1_out, and_2_out);
  or or_2 (K2, and_3_out, and_4_out);
endmodule

module FF1 (
  input  Start,
  input  RO,
  input  E2,
  input  E0,
  input  CH,
  input  CQ,
  input  PG,
  output J1,
  output K1
);

  wire and_1_out, and_2_out, and_3_out, and_4_out, and_5_out, not_1_out, not_2_out, not_3_out, not_4_out,
       not_5_out;

  not not_1 (not_1_out, E0);
  not not_2 (not_2_out, E2);
  not not_3 (not_3_out, E0);
  not not_4 (not_4_out, E2);
  not not_5 (not_5_out, E2);
  and and_1 (and_1_out, Start, CQ, E2, not_1_out);
  and and_2 (and_2_out, Start, PG, not_2_out, E0);
  and and_3 (and_3_out, Start, E2, not_3_out);
  and and_4 (and_4_out, Start, RO, not_4_out, E0);
  and and_5 (and_5_out, Start, CH, RO, not_5_out);
  or or_1 (J1, and_1_out, and_2_out);
  or or_2 (K1, and_3_out, and_4_out, and_5_out);
endmodule

module FF0 (
  input  Start,
  input  RO,
  input  E2,
  input  E1,
  input  E0,
  input  CH,
  input  CQ,
  input  PG,
  input  EB,
  output J0,
  output K0
);

  wire and_1_out, and_2_out, and_3_out, and_4_out, and_5_out, and_6_out, not_1_out, not_2_out, not_3_out,
       not_4_out, not_5_out, not_6_out, not_7_out, not_8_out, not_9_out, not_10_out, not_11_out;

  not not_1 (not_1_out, CQ);
  not not_2 (not_2_out, E1);
  not not_3 (not_3_out, PG);
  not not_4 (not_4_out, EB);
  not not_5 (not_5_out, E2);
  not not_6 (not_6_out, E1);
  not not_7 (not_7_out, RO);
  not not_8 (not_8_out, E2);
  not not_9 (not_9_out, E1);
  not not_10 (not_10_out, E2);
  not not_11 (not_11_out, E1);
  and and_1 (and_1_out, Start, not_1_out, E2, not_2_out);
  and and_2 (and_2_out, Start, not_3_out, not_4_out, not_5_out, not_6_out);
  and and_3 (and_3_out, Start, CH, not_7_out, not_8_out, E1);
  and and_4 (and_4_out, Start, E2, not_9_out);
  and and_5 (and_5_out, Start, RO, not_10_out, E1);
  and and_6 (and_6_out, Start, PG, not_11_out);
  or or_1 (J0, and_1_out, and_2_out, and_3_out);
  or or_2 (K0, and_4_out, and_5_out, and_6_out);
endmodule

module Circuito_de_Saida (
  input  Start,
  input  RO,
  input  E2,
  input  E1,
  input  E0,
  input  CH,
  input  PG,
  input  CQ,
  input  EB,
  output MOTOR,
  output EV,
  output VE,
  output ALARME
);

  wire and_1_out, and_2_out, and_3_out, and_4_out, and_5_out, and_6_out, and_7_out, and_8_out, and_9_out,
       and_10_out, and_11_out, and_12_out, not_1_out, not_2_out, not_3_out, not_4_out, not_5_out, not_6_out,
       not_7_out, not_8_out, not_9_out, not_10_out, not_11_out, not_12_out, not_13_out, not_14_out,
       not_15_out, not_16_out, not_17_out, not_18_out, not_19_out, not_20_out;

  not not_1 (not_1_out, PG);
  not not_2 (not_2_out, EB);
  not not_3 (not_3_out, E1);
  not not_4 (not_4_out, E0);
  not not_5 (not_5_out, PG);
  not not_6 (not_6_out, E1);
  not not_7 (not_7_out, E1);
  not not_8 (not_8_out, E2);
  not not_9 (not_9_out, E2);
  not not_10 (not_10_out, CH);
  not not_11 (not_11_out, E2);
  not not_12 (not_12_out, E0);
  not not_13 (not_13_out, E2);
  not not_14 (not_14_out, E1);
  not not_15 (not_15_out, E2);
  not not_16 (not_16_out, E2);
  not not_17 (not_17_out, RO);
  not not_18 (not_18_out, E2);
  not not_19 (not_19_out, RO);
  not not_20 (not_20_out, E2);
  and and_1 (and_1_out, Start, not_1_out, not_2_out, not_3_out);
  and and_2 (and_2_out, Start, E2, not_4_out);
  and and_3 (and_3_out, Start, not_5_out, not_6_out, E0);
  and and_4 (and_4_out, Start, E2, not_7_out);
  and and_5 (and_5_out, Start, RO, not_8_out, E1, E0);
  and and_6 (and_6_out, Start, CH, RO, not_9_out, E1);
  and and_7 (and_7_out, Start, not_10_out, not_11_out, E1, not_12_out);
  and and_8 (and_8_out, Start, PG, not_13_out, not_14_out, E0);
  and and_9 (and_9_out, Start, RO, not_15_out, E1, E0);
  and and_10 (and_10_out, Start, CH, RO, not_16_out, E1);
  and and_11 (and_11_out, Start, not_17_out, not_18_out, E1, E0);
  and and_12 (and_12_out, Start, CH, not_19_out, not_20_out, E1);
  or or_1 (MOTOR, and_1_out, and_2_out, and_3_out, and_4_out, and_5_out, and_6_out);
  or or_2 (EV, and_7_out, and_8_out);
  or or_3 (VE, and_9_out, and_10_out);
  or or_4 (ALARME, and_11_out, and_12_out);
endmodule
