// Logisim project projeto.circ as structural Verilog: 9 circuits, main circuit main
module main (
  input  Start,
  input  PG,
  input  CH,
  input  RO,
  input  CQ,
  input  EB,
  input  Incrementar_Rolha,
  output E2,
  output E1,
  output E0
);

  wire and_1_out, and_2_out, and_3_out, Clock_out, Contador_0_99_2_m0, Contador_0_99_2_m1,
       Contador_0_99_2_m2, Contador_0_99_2_m3, Contador_0_99_2_s0, Contador_0_99_2_s1, Contador_0_99_2_s2,
       Contador_0_99_2_s3, Contador_0_99_m0, Contador_0_99_m1, Contador_0_99_m2, Contador_0_99_m3,
       Contador_0_99_s0, Contador_0_99_s1, Contador_0_99_s2, Contador_0_99_s3, Contador_de_Duzias_s0,
       Contador_de_Duzias_s1, Contador_de_Duzias_s2, Contador_de_Duzias_s3, Decodificador_0_9_2_a_2,
       Decodificador_0_9_2_b_2, Decodificador_0_9_2_c_2, Decodificador_0_9_2_d_2, Decodificador_0_9_2_dp,
       Decodificador_0_9_2_e, Decodificador_0_9_2_f, Decodificador_0_9_2_g, Decodificador_0_9_3_a_2,
       Decodificador_0_9_3_b_2, Decodificador_0_9_3_c_2, Decodificador_0_9_3_d_2, Decodificador_0_9_3_dp,
       Decodificador_0_9_3_e, Decodificador_0_9_3_f, Decodificador_0_9_3_g, Decodificador_0_9_4_a_2,
       Decodificador_0_9_4_b_2, Decodificador_0_9_4_c_2, Decodificador_0_9_4_d_2, Decodificador_0_9_4_dp,
       Decodificador_0_9_4_e, Decodificador_0_9_4_f, Decodificador_0_9_4_g, Decodificador_0_9_a_2,
       Decodificador_0_9_b_2, Decodificador_0_9_c_2, Decodificador_0_9_d_2, Decodificador_0_9_dp,
       Decodificador_0_9_e, Decodificador_0_9_f, Decodificador_0_9_g, MEF_Principal_alarme, MEF_Principal_ev,
       MEF_Principal_motor, MEF_Principal_ve, or_1_out, or_2_out, or_3_out;

  Clock Clock (.out(Clock_out));
  mef_principal_main MEF_Principal (
    .Clock(Clock_out), .Start(Start), .PG(PG), .CH(CH), .RO(RO), .CQ(CQ), .EB(EB), .E2(E2), .E1(E1), .E0(E0),
    .MOTOR(MEF_Principal_motor), .EV(MEF_Principal_ev), .VE(MEF_Principal_ve), .ALARME(MEF_Principal_alarme));
  and and_1 (and_1_out, E2, E1, ~E0);  // AND_Gate
  LED Motor (.in(MEF_Principal_motor));
  LED EV (.in(MEF_Principal_ev));
  LED VE (.in(MEF_Principal_ve));
  LED Alarme (.in(MEF_Principal_alarme));
  LED u_PG (.in(PG));
  LED u_CH (.in(CH));
  LED u_RO (.in(RO));
  LED u_CQ (.in(CQ));
  LED u_EB (.in(EB));
  LED u_Start (.in(Start));
  contador_de_duzias___mef Contador_de_Duzias (
    .Clock(and_1_out), .Reset(and_2_out), .S3(Contador_de_Duzias_s3), .S2(Contador_de_Duzias_s2),
    .S1(Contador_de_Duzias_s1), .S0(Contador_de_Duzias_s0));
  and and_2 (and_2_out, Contador_de_Duzias_s3, Contador_de_Duzias_s2, ~Contador_de_Duzias_s1, ~Contador_de_Duzias_s0);  // AND_Gate
  or or_1 (or_1_out, ~Start, and_3_out);  // OR_Gate
  and and_3 (and_3_out, ~Contador_0_99_m3, ~Contador_0_99_m2, ~Contador_0_99_m1, ~Contador_0_99_m0, ~Contador_0_99_s3, ~Contador_0_99_s2, ~Contador_0_99_s1, Contador_0_99_s0);  // AND_Gate
  or or_2 (or_2_out, MEF_Principal_ve, Incrementar_Rolha);
  or or_3 (or_3_out, ~MEF_Principal_ve, Incrementar_Rolha);  // OR_Gate
  Contador_0_99 Contador_0_99 (
    .Clock(and_2_out), .I(1'b1), .Reset(or_1_out), .M3(Contador_0_99_m3), .M2(Contador_0_99_m2),
    .M1(Contador_0_99_m1), .M0(Contador_0_99_m0), .S3(Contador_0_99_s3), .S2(Contador_0_99_s2),
    .S1(Contador_0_99_s1), .S0(Contador_0_99_s0));  // open: Auto_Repor
  Contador_0_99 Contador_0_99_2 (
    .Clock(or_2_out), .I(or_3_out), .Auto_Repor(1'b1), .M3(Contador_0_99_2_m3), .M2(Contador_0_99_2_m2),
    .M1(Contador_0_99_2_m1), .M0(Contador_0_99_2_m0), .S3(Contador_0_99_2_s3), .S2(Contador_0_99_2_s2),
    .S1(Contador_0_99_2_s1), .S0(Contador_0_99_2_s0));  // open: Reset
  decod_num_0_9 Decodificador_0_9 (
    .a(Contador_0_99_s3), .b(Contador_0_99_s2), .c(Contador_0_99_s1), .d(Contador_0_99_s0),
    .A_2(Decodificador_0_9_a_2), .B_2(Decodificador_0_9_b_2), .C_2(Decodificador_0_9_c_2),
    .D_2(Decodificador_0_9_d_2), .E(Decodificador_0_9_e), .F(Decodificador_0_9_f), .G(Decodificador_0_9_g),
    .DP(Decodificador_0_9_dp));
  decod_num_0_9 Decodificador_0_9_2 (
    .a(Contador_0_99_m3), .b(Contador_0_99_m2), .c(Contador_0_99_m1), .d(Contador_0_99_m0),
    .A_2(Decodificador_0_9_2_a_2), .B_2(Decodificador_0_9_2_b_2), .C_2(Decodificador_0_9_2_c_2),
    .D_2(Decodificador_0_9_2_d_2), .E(Decodificador_0_9_2_e), .F(Decodificador_0_9_2_f),
    .G(Decodificador_0_9_2_g), .DP(Decodificador_0_9_2_dp));
  decod_num_0_9 Decodificador_0_9_3 (
    .a(Contador_0_99_2_s3), .b(Contador_0_99_2_s2), .c(Contador_0_99_2_s1), .d(Contador_0_99_2_s0),
    .A_2(Decodificador_0_9_3_a_2), .B_2(Decodificador_0_9_3_b_2), .C_2(Decodificador_0_9_3_c_2),
    .D_2(Decodificador_0_9_3_d_2), .E(Decodificador_0_9_3_e), .F(Decodificador_0_9_3_f),
    .G(Decodificador_0_9_3_g), .DP(Decodificador_0_9_3_dp));
  decod_num_0_9 Decodificador_0_9_4 (
    .a(Contador_0_99_2_m3), .b(Contador_0_99_2_m2), .c(Contador_0_99_2_m1), .d(Contador_0_99_2_m0),
    .A_2(Decodificador_0_9_4_a_2), .B_2(Decodificador_0_9_4_b_2), .C_2(Decodificador_0_9_4_c_2),
    .D_2(Decodificador_0_9_4_d_2), .E(Decodificador_0_9_4_e), .F(Decodificador_0_9_4_f),
    .G(Decodificador_0_9_4_g), .DP(Decodificador_0_9_4_dp));
  _7_Segment_Display #(.active("false")) u_7_segment_display_1 (
    .g(Decodificador_0_9_g), .f(Decodificador_0_9_f), .a(Decodificador_0_9_a_2), .b(Decodificador_0_9_b_2),
    .e(Decodificador_0_9_e), .d(Decodificador_0_9_d_2), .c(Decodificador_0_9_c_2), .dp(Decodificador_0_9_dp));
  _7_Segment_Display #(.active("false")) u_7_segment_display_2 (
    .g(Decodificador_0_9_2_g), .f(Decodificador_0_9_2_f), .a(Decodificador_0_9_2_a_2),
    .b(Decodificador_0_9_2_b_2), .e(Decodificador_0_9_2_e), .d(Decodificador_0_9_2_d_2),
    .c(Decodificador_0_9_2_c_2), .dp(Decodificador_0_9_2_dp));
  _7_Segment_Display #(.active("false")) u_7_segment_display_3 (
    .g(Decodificador_0_9_3_g), .f(Decodificador_0_9_3_f), .a(Decodificador_0_9_3_a_2),
    .b(Decodificador_0_9_3_b_2), .e(Decodificador_0_9_3_e), .d(Decodificador_0_9_3_d_2),
    .c(Decodificador_0_9_3_c_2), .dp(Decodificador_0_9_3_dp));
  _7_Segment_Display #(.active("false")) u_7_segment_display_4 (
    .g(Decodificador_0_9_4_g), .f(Decodificador_0_9_4_f), .a(Decodificador_0_9_4_a_2),
    .b(Decodificador_0_9_4_b_2), .e(Decodificador_0_9_4_e), .d(Decodificador_0_9_4_d_2),
    .c(Decodificador_0_9_4_c_2), .dp(Decodificador_0_9_4_dp));

  // Notes on the sheet:
  //   Duzias
  //   Rolhas
endmodule

module decod_num_0_9 (
  input  a,
  input  b,
  input  c,
  input  d,
  output A_2,
  output B_2,
  output C_2,
  output D_2,
  output E,
  output F,
  output G,
  output DP
);

  wire and_1_out, and_2_out, and_3_out, and_4_out, and_5_out, and_6_out, and_7_out, and_8_out, and_9_out,
       and_10_out, and_11_out, and_12_out, and_13_out, and_14_out, and_15_out, and_16_out, and_17_out,
       and_18_out, and_19_out, and_20_out, and_21_out, and_22_out, and_23_out, and_24_out, and_25_out,
       and_26_out, not_1_out, not_2_out, not_3_out, not_4_out, not_5_out, not_6_out, not_7_out, not_8_out,
       not_9_out, not_10_out, not_11_out, not_12_out, not_13_out, not_14_out, not_15_out, not_16_out,
       not_17_out, not_18_out, not_19_out, not_20_out, not_21_out;

  not not_1 (not_1_out, a);
  not not_2 (not_2_out, b);
  not not_3 (not_3_out, c);
  not not_4 (not_4_out, c);
  not not_5 (not_5_out, d);
  and and_1 (and_1_out, a, b);
  and and_2 (and_2_out, a, c);
  and and_3 (and_3_out, b, c, not_6_out);
  not not_6 (not_6_out, d);
  and and_4 (and_4_out, b, not_7_out, d);
  not not_7 (not_7_out, c);
  and and_5 (and_5_out, a, b);
  and and_6 (and_6_out, a, c);
  not not_8 (not_8_out, b);
  and and_7 (and_7_out, not_8_out, c, not_9_out);
  not not_9 (not_9_out, d);
  not not_10 (not_10_out, a);
  not not_11 (not_11_out, b);
  not not_12 (not_12_out, c);
  not not_13 (not_13_out, c);
  not not_14 (not_14_out, d);
  and and_8 (and_8_out, a, c);
  and and_9 (and_9_out, b, not_15_out);
  not not_15 (not_15_out, c);
  and and_10 (and_10_out, a, b);
  not not_16 (not_16_out, a);
  not not_17 (not_17_out, b);
  and and_11 (and_11_out, not_16_out, not_17_out, d);
  not not_18 (not_18_out, b);
  and and_12 (and_12_out, not_18_out, c);
  and and_13 (and_13_out, c, d);
  and and_14 (and_14_out, a, b);
  and and_15 (and_15_out, a, c);
  not not_19 (not_19_out, a);
  not not_20 (not_20_out, b);
  and and_16 (and_16_out, not_19_out, not_20_out, not_21_out);
  not not_21 (not_21_out, c);
  and and_17 (and_17_out, b, c, d);
  and and_18 (and_18_out, a, b);
  and and_19 (and_19_out, a, c);
  and and_20 (and_20_out, not_1_out, not_2_out, not_3_out, d);
  and and_21 (and_21_out, b, not_4_out, not_5_out);
  or or_1 (B_2, and_1_out, and_2_out, and_3_out, and_4_out);
  or or_2 (C_2, and_5_out, and_6_out, and_7_out);
  and and_22 (and_22_out, a, b);
  and and_23 (and_23_out, a, c);
  and and_24 (and_24_out, not_10_out, not_11_out, not_12_out, d);
  and and_25 (and_25_out, b, c, d);
  and and_26 (and_26_out, b, not_13_out, not_14_out);
  or or_3 (E, and_8_out, and_9_out, d);
  or or_4 (F, and_10_out, and_11_out, and_12_out, and_13_out);
  or or_5 (G, and_14_out, and_15_out, and_16_out, and_17_out);
  or or_6 (A_2, and_18_out, and_19_out, and_20_out, and_21_out);
  or or_7 (D_2, and_22_out, and_23_out, and_24_out, and_25_out, and_26_out);

  assign DP = 1'b1;
endmodule

module \Lógica_de_Estado_Próximo  (
  input  a,
  input  b,
  input  c,
  input  d,
  output k0,
  output j0,
  output k1,
  output j1,
  output k2,
  output j2,
  output k3,
  output j3
);

  wire and_1_out, and_2_out, and_3_out, and_4_out, and_5_out, and_6_out, not_1_out, not_2_out, not_3_out,
       not_4_out, not_5_out, not_6_out, not_7_out, not_8_out, not_9_out, not_10_out, not_11_out, not_12_out,
       not_13_out, not_14_out, not_15_out;

  not not_1 (not_1_out, a);
  or or_1 (k0, not_1_out, not_2_out);
  not not_2 (not_2_out, b);
  not not_3 (not_3_out, a);
  or or_2 (j0, not_3_out, not_4_out);
  not not_4 (not_4_out, b);
  not not_5 (not_5_out, a);
  and and_1 (and_1_out, not_5_out, d);
  not not_6 (not_6_out, b);
  and and_2 (and_2_out, not_6_out, d);
  not not_7 (not_7_out, a);
  and and_3 (and_3_out, not_7_out, d);
  not not_8 (not_8_out, b);
  and and_4 (and_4_out, not_8_out, d);
  not not_9 (not_9_out, a);
  and and_5 (and_5_out, not_9_out, c, d);
  not not_10 (not_10_out, c);
  and and_6 (and_6_out, a, not_10_out, not_11_out);
  not not_11 (not_11_out, d);
  not not_12 (not_12_out, b);
  and and_7 (j2, not_12_out, c, d);
  not not_13 (not_13_out, c);
  and and_8 (k3, b, not_13_out, not_14_out);
  not not_14 (not_14_out, d);
  not not_15 (not_15_out, a);
  or or_3 (k1, and_1_out, and_2_out);
  or or_4 (j1, and_3_out, and_4_out);
  or or_5 (k2, and_5_out, and_6_out);
  and and_9 (j3, not_15_out, b, c, d);
endmodule

module contador_de_duzias___mef (
  input  Clock,
  input  Reset,
  output S3,
  output S2,
  output S1,
  output S0
);

  wire \lógica_de_estado_próximo_1_j0 , \lógica_de_estado_próximo_1_j1 , \lógica_de_estado_próximo_1_j2 ,
       \lógica_de_estado_próximo_1_j3 , \lógica_de_estado_próximo_1_k0 , \lógica_de_estado_próximo_1_k1 ,
       \lógica_de_estado_próximo_1_k2 , \lógica_de_estado_próximo_1_k3 ;

  \Lógica_de_Estado_Próximo  \lógica_de_estado_próximo_1  (
    .a(S3), .b(S2), .c(S1), .d(S0), .k0(\lógica_de_estado_próximo_1_k0 ),
    .j0(\lógica_de_estado_próximo_1_j0 ), .k1(\lógica_de_estado_próximo_1_k1 ),
    .j1(\lógica_de_estado_próximo_1_j1 ), .k2(\lógica_de_estado_próximo_1_k2 ),
    .j2(\lógica_de_estado_próximo_1_j2 ), .k3(\lógica_de_estado_próximo_1_k3 ),
    .j3(\lógica_de_estado_próximo_1_j3 ));
  J_K_Flip_Flop j_k_ff_1 (
    .J(\lógica_de_estado_próximo_1_j3 ), .clk(Clock), .K(\lógica_de_estado_próximo_1_k3 ), .Q(S3),
    .reset(Reset));  // open: Qn, preset, en
  J_K_Flip_Flop j_k_ff_2 (
    .J(\lógica_de_estado_próximo_1_j2 ), .clk(Clock), .K(\lógica_de_estado_próximo_1_k2 ), .Q(S2),
    .reset(Reset));  // open: Qn, preset, en
  J_K_Flip_Flop j_k_ff_3 (
    .J(\lógica_de_estado_próximo_1_j1 ), .clk(Clock), .K(\lógica_de_estado_próximo_1_k1 ), .Q(S1),
    .reset(Reset));  // open: Qn, preset, en
  J_K_Flip_Flop j_k_ff_4 (
    .J(\lógica_de_estado_próximo_1_j0 ), .clk(Clock), .K(\lógica_de_estado_próximo_1_k0 ), .Q(S0),
    .reset(Reset));  // open: Qn, preset, en
endmodule

module lep___contador_c_d (
  input  a,
  input  b,
  input  c,
  input  d,
  input  i,
  output k0,
  output j0,
  output k1,
  output j1,
  output k2,
  output j2,
  output k3,
  output j3
);

  wire and_1_out, and_2_out, and_3_out, and_4_out, and_5_out, and_6_out, and_7_out, and_8_out, and_9_out,
       and_10_out, and_11_out, and_12_out, and_13_out, and_14_out, and_15_out, not_1_out, not_2_out,
       not_3_out, not_4_out, not_5_out, not_6_out, not_7_out, not_8_out, not_9_out, not_10_out, not_11_out,
       not_12_out, not_13_out, not_14_out, not_15_out, not_16_out, not_17_out, not_18_out, not_19_out,
       not_20_out, not_21_out, not_22_out, not_23_out, not_24_out, not_25_out, not_26_out, not_27_out,
       not_28_out, not_29_out, not_30_out, not_31_out, not_32_out, not_33_out, not_34_out, not_35_out,
       not_36_out, not_37_out, not_38_out, not_39_out;

  not not_1 (not_1_out, b);
  not not_2 (not_2_out, c);
  not not_3 (not_3_out, b);
  not not_4 (not_4_out, c);
  not not_5 (not_5_out, i);
  not not_6 (not_6_out, a);
  not not_7 (not_7_out, d);
  not not_8 (not_8_out, a);
  not not_9 (not_9_out, i);
  not not_10 (not_10_out, a);
  not not_11 (not_11_out, d);
  not not_12 (not_12_out, i);
  not not_13 (not_13_out, b);
  not not_14 (not_14_out, c);
  not not_15 (not_15_out, d);
  not not_16 (not_16_out, a);
  not not_17 (not_17_out, i);
  not not_18 (not_18_out, a);
  not not_19 (not_19_out, c);
  not not_20 (not_20_out, d);
  not not_21 (not_21_out, a);
  not not_22 (not_22_out, i);
  not not_23 (not_23_out, b);
  not not_24 (not_24_out, c);
  not not_25 (not_25_out, d);
  not not_26 (not_26_out, a);
  not not_27 (not_27_out, i);
  not not_28 (not_28_out, b);
  not not_29 (not_29_out, c);
  not not_30 (not_30_out, d);
  not not_31 (not_31_out, b);
  not not_32 (not_32_out, c);
  not not_33 (not_33_out, i);
  not not_34 (not_34_out, b);
  not not_35 (not_35_out, c);
  not not_36 (not_36_out, d);
  not not_37 (not_37_out, a);
  not not_38 (not_38_out, a);
  and and_1 (and_1_out, not_1_out, not_2_out);
  not not_39 (not_39_out, a);
  and and_2 (and_2_out, not_3_out, not_4_out);
  and and_3 (and_3_out, not_5_out, not_6_out, not_7_out);
  and and_4 (and_4_out, i, not_8_out, d);
  and and_5 (and_5_out, not_9_out, not_10_out, b, not_11_out);
  and and_6 (and_6_out, not_12_out, a, not_13_out, not_14_out, not_15_out);
  and and_7 (and_7_out, i, not_16_out, d);
  and and_8 (and_8_out, not_17_out, not_18_out, not_19_out, not_20_out);
  and and_9 (and_9_out, i, not_21_out, c, d);
  and and_10 (and_10_out, not_22_out, a, not_23_out, not_24_out, not_25_out);
  and and_11 (and_11_out, i, not_26_out, c, d);
  and and_12 (and_12_out, not_27_out, not_28_out, not_29_out, not_30_out);
  and and_13 (and_13_out, i, not_31_out, not_32_out, d);
  and and_14 (and_14_out, not_33_out, not_34_out, not_35_out, not_36_out);
  and and_15 (and_15_out, i, not_37_out, b, c, d);
  or or_1 (k0, not_38_out, and_1_out);
  or or_2 (j0, not_39_out, and_2_out);
  or or_3 (k1, and_3_out, and_4_out);
  or or_4 (j1, and_5_out, and_6_out, and_7_out);
  or or_5 (k2, and_8_out, and_9_out);
  or or_6 (j2, and_10_out, and_11_out);
  or or_7 (k3, and_12_out, and_13_out);
  or or_8 (j3, and_14_out, and_15_out);
endmodule

module Contador_C_D (
  input  Clock,
  input  I,
  input  Reset,
  input  _2,
  input  _5,
  output S3,
  output S2,
  output S1,
  output S0
);

  wire lep_contador_c_d_1_j0, lep_contador_c_d_1_j1, lep_contador_c_d_1_j2, lep_contador_c_d_1_j3,
       lep_contador_c_d_1_k0, lep_contador_c_d_1_k1, lep_contador_c_d_1_k2, lep_contador_c_d_1_k3, or_1_out,
       or_2_out, or_3_out, or_4_out;

  lep___contador_c_d lep_contador_c_d_1 (
    .a(S3), .b(S2), .c(S1), .d(S0), .i(I), .k0(lep_contador_c_d_1_k0), .j0(lep_contador_c_d_1_j0),
    .k1(lep_contador_c_d_1_k1), .j1(lep_contador_c_d_1_j1), .k2(lep_contador_c_d_1_k2),
    .j2(lep_contador_c_d_1_j2), .k3(lep_contador_c_d_1_k3), .j3(lep_contador_c_d_1_j3));
  or or_1 (or_1_out, Reset, _5, _2);
  or or_2 (or_2_out, Reset, _2);
  or or_3 (or_3_out, Reset, _5);
  or or_4 (or_4_out, Reset, _2);
  J_K_Flip_Flop j_k_ff_1 (
    .J(lep_contador_c_d_1_j3), .clk(Clock), .K(lep_contador_c_d_1_k3), .Q(S3), .reset(or_1_out));  // open: Qn, preset, en
  J_K_Flip_Flop j_k_ff_2 (
    .J(lep_contador_c_d_1_j2), .clk(Clock), .K(lep_contador_c_d_1_k2), .Q(S2), .preset(_5), .reset(or_2_out));  // open: Qn, en
  J_K_Flip_Flop j_k_ff_3 (
    .J(lep_contador_c_d_1_j1), .clk(Clock), .K(lep_contador_c_d_1_k1), .Q(S1), .preset(_2), .reset(or_3_out));  // open: Qn, en
  J_K_Flip_Flop j_k_ff_4 (
    .J(lep_contador_c_d_1_j0), .clk(Clock), .K(lep_contador_c_d_1_k0), .Q(S0), .preset(_5), .reset(or_4_out));  // open: Qn, en
endmodule

module Contador_0_99 (
  input  Clock,
  input  I,
  input  Reset,
  input  Auto_Repor,
  output M3,
  output M2,
  output M1,
  output M0,
  output S3,
  output S2,
  output S1,
  output S0
);

  wire and_1_out, and_2_out, and_3_out, and_4_out, eh_nove_1_s, eh_nove_2_s, menor_que_cinco_1_s,
       multiplexer_1_out, not_1_out;

  and and_1 (and_1_out, ~and_4_out, Clock);  // AND_Gate
  Contador_C_D unidades (
    .Clock(and_1_out), .I(I), .Reset(Reset), ._5(and_2_out), .S3(M3), .S2(M2), .S1(M1), .S0(M0));  // open: _2
  not not_1 (not_1_out, M3);
  Multiplexer #(.enable("false")) multiplexer_1 (.in0(M3), .in1(not_1_out), .out(multiplexer_1_out), .sel(I));
  Contador_C_D dezenas (
    .Clock(multiplexer_1_out), .I(I), .Reset(Reset), ._2(and_2_out), .S3(S3), .S2(S2), .S1(S1), .S0(S0));  // open: _5
  and and_2 (and_2_out, Auto_Repor, menor_que_cinco_1_s, and_3_out);
  menor_que_cinco menor_que_cinco_1 (.a(M3), .b(M2), .c(M1), .d(M0), .S(menor_que_cinco_1_s));
  and and_3 (and_3_out, ~S3, ~S2, ~S1, ~S0);  // AND_Gate
  and and_4 (and_4_out, eh_nove_1_s, eh_nove_2_s);
  eh_nove eh_nove_1 (.a(M3), .b(M2), .c(M1), .d(M0), .S(eh_nove_1_s));
  eh_nove eh_nove_2 (.a(S3), .b(S2), .c(S1), .d(S0), .S(eh_nove_2_s));
endmodule

module menor_que_cinco (
  input  a,
  input  b,
  input  c,
  input  d,
  output S
);

  wire and_1_out, and_2_out, not_1_out, not_2_out, not_3_out, not_4_out;

  not not_1 (not_1_out, a);
  and and_1 (and_1_out, not_1_out, not_2_out);
  not not_2 (not_2_out, b);
  not not_3 (not_3_out, a);
  and and_2 (and_2_out, not_3_out, not_4_out);
  not not_4 (not_4_out, c);
  or or_1 (S, and_1_out, and_2_out);
endmodule

module eh_nove (
  input  a,
  input  b,
  input  c,
  input  d,
  output S
);

  wire not_1_out, not_2_out;

  not not_1 (not_1_out, b);
  not not_2 (not_2_out, c);
  and and_1 (S, a, not_1_out, not_2_out, d);
endmodule
